# Fritzing sketch RFDuinoMicDevice (saved by Fritzing 0.9.3b)
breadboards: 1

parts:
  RFduinoSMD1 = RFduino SMD
  VCC1 = Battery
  Part1 = Adafruit MAX4466 Electret Microphone Amplifier [part_number="Adafruit #1063"]

nets:
  GND: RFduinoSMD1.gnd, VCC1.+, Part1.GND
  VIN: RFduinoSMD1.vin, VCC1.-, Part1.VCC
  N1: RFduinoSMD1.gpio6, Part1.OUT

custom parts:
  Adafruit MAX4466 Electret Microphone Amplifier: Add an ear to your project with this well-designed electret microphone amplifier. This fully assembled and tested board comes with a 20-20KHz electret microphone soldered on. For the amplification, we use the Maxim MAX4466, an op-amp specifically designed for this delicate task! The amplifier has excellent power supply noise rejection, so this amplifier sounds really good and isn't nearly as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
